# Fritzing sketch photon_dht11_sketch (saved by Fritzing 0.9.3b)
breadboards: 1

parts:
  Part1 = Photon
  DHT2 = DHT11 Humitidy and Temperature Sensor (3 pins)

nets:
  GND: Part1.GND, DHT2.GND
  N1: Part1.D2, DHT2.DATA
  3V3: Part1.3V3, DHT2.VDD

custom parts:
  DHT11 Humitidy and Temperature Sensor (3 pins): DHT11 Humidity and Temperature Sensor (3 pins) from the design created by John De Cristofaro for Adafruit Industries.
